# Fritzing sketch controller (saved by Fritzing 0.7.10b)
breadboards: 1

parts:
  Teensy1 = Teensy 2.0
  VCC1 = 4 x AAA Battery Mount
  L293D = L293D [package=THT]
  M1 = DC Motor
  M2 = DC Motor
  R1 = 390 Ω Resistor [package=THT]
  R2 = 390 Ω Resistor [package=THT]
  Q2 = NPN-Transistor [package="TO92 [THT]"]
  Q3 = NPN-Transistor [package="TO92 [THT]"]
  LED1 = LED - 3mm [color="Red (633nm)" package="3 mm [THT]"]
  LED2 = LED - 3mm [color="Red (633nm)" package="3 mm [THT]"]

nets:
  N1: Teensy1.GND, VCC1.-, L293D.0V, LED1.cathode, LED2.cathode
  N2: Teensy1.B5, R2.Pin_0
  N3: Teensy1.B6, R1.Pin_0
  N4: Teensy1.F7, L293D.In_2
  N5: Teensy1.F6, L293D.In_1
  N6: Teensy1.F5, L293D.Enable_1
  N7: Teensy1.F4, L293D.In_3
  N8: Teensy1.F1, L293D.In_4
  N9: Teensy1.F0, L293D.Enable_2
  N10: Teensy1.VCC, L293D.+V
  N11: VCC1.+, L293D.+Vmotor, Q2.C, Q3.C
  N12: L293D.Out_1_(_Controlled_by_Enable_1_), M1.pin_2
  N13: L293D.Out_2_(_Controlled_by_Enable_1_), M1.pin_1
  N14: L293D.Out_3_(_Controlled_by_Enable_2_), M2.pin_2
  N15: L293D.Out_4_(_Controlled_by_Enable_2_), M2.pin_1
  N16: R1.Pin_1, Q2.B
  N17: R2.Pin_1, Q3.B
  N18: Q2.E, LED1.anode
  N19: Q3.E, LED2.anode

custom parts:
  390 Ω Resistor: A generic resistor (0.25W)
